// Logisim project dmh148_project3.circ as structural Verilog: 6 circuits, main circuit main
module main (
);

  wire Clock, clock_1_out, HALT, Itype, MEM, not_1_p1, not_2_out, not_3_out, put, Rwe, WE;
  wire [1:0] PC;
  wire [2:0] ALUOp, RSGet, RTGet, WDOp;
  wire [3:0] display_1_digits_1, display_1_digits_2, display_1_digits_3, display_1_digits_4;
  wire [6:0] halt_2_out_2, halt_2_out_3, halt_2_out_4, halt_2_out_5, halt_2_out_6, halt_2_out_7,
       halt_2_out_8, halt_2_out_9, halt_2_out_10, halt_2_out_11, halt_2_out_12, halt_2_out_13, halt_2_out_14,
       halt_2_out_15, halt_2_out_16, halt_2_out_17;
  wire [7:0] adder_1_out, adder_2_out, controlled_buffer_1_out, multiplexer_1_out, register_1_q;
  wire [15:0] ALUout, Data, Imm, Inst, multiplexer_2_out, multiplexer_3_out, PC_1, Rem, RS, RT;

  Adder adder_1 (.a(register_1_q), .b(8'h1), .out(adder_1_out));  // open: cin, cout
  Multiplexer #(.select(2), .width(8)) multiplexer_1 (
    .in0(adder_1_out), .in1(Imm[7:0]), .in2(RS[7:0]), .out(multiplexer_1_out), .sel(PC));  // open: in3, en
  // NOT_Gate not_1: pin names not known; wires that end beside it: not_1_p1, HALT
  Adder adder_2 (.a(register_1_q), .b(8'h1), .out(adder_2_out));  // open: cin, cout
  Multiplexer #(.select(3), .width(16)) multiplexer_2 (
    .in0(ALUout), .in1(ALUout), .in2(Imm), .in3(PC_1), .in4(Data), .out(multiplexer_2_out), .sel(WDOp));  // open: in5, in6, in7, en
  // NOT_Gate not_2 has open pins: in=open, out=not_2_out
  Register register_1 (.D(multiplexer_1_out), .en(not_1_p1), .Q(register_1_q), .clk(Clock));  // open: clr
  assign controlled_buffer_1_out = not_2_out ? register_1_q : 8'bz;  // Controlled_Buffer controlled_buffer_1
  assign PC_1 = {{8{adder_2_out[7]}}, adder_2_out};  // Bit_Extender bit_extender_1
  RAM #(.dataWidth(16), .bus("separate")) ram_1 (
    .addr(RT[7:0]), .din(RS), .data(Data), .sel(MEM), .clk(Clock));  // open: str, ld, clr
  register_file register_file_1 (
    .WriteEnable(WE), .WireData(multiplexer_2_out), .ReadRegister1(RSGet), .ReadRegister2(RTGet),
    .WriteRegister(RSGet), .Clock(Clock), .WireData_1(Rem), .WriteEnable_1(Rwe), .ReadData1(RS),
    .ReadData2(RT));
  // NOT_Gate not_3 has open pins: in=open, out=not_3_out
  Clock clock_1 (.out(clock_1_out));
  assign Clock = not_3_out ? clock_1_out : 1'bz;  // Controlled_Buffer controlled_buffer_2
  ROM #(.dataWidth(16)) rom_1 (.addr(controlled_buffer_1_out), .data(Inst));  // open: sel
  Control control_1 (
    .Halt(HALT), .Instruction(Inst), .RT(RTGet), .Put(put), .RS(RSGet), .I_Type(Itype), .Immediate(Imm),
    .ALUOp(ALUOp), .DoMem(MEM), .PC(PC), .WriteEnable(WE), .RSin(RS), .WriteOp(WDOp));
  LED u_HALT (.in(HALT));
  Hex_Digit_Display hex_digit_display_1 (.value(display_1_digits_3));  // open: dp
  Hex_Digit_Display hex_digit_display_2 (.value(display_1_digits_4));  // open: dp
  DotMatrix #(.matrixcols(16)) dotmatrix_1 (
    .col0(halt_2_out_2), .col1(halt_2_out_3), .col2(halt_2_out_4), .col3(halt_2_out_5), .col4(halt_2_out_6),
    .col5(halt_2_out_7), .col6(halt_2_out_8), .col7(halt_2_out_9), .col8(halt_2_out_10),
    .col9(halt_2_out_11), .col10(halt_2_out_12), .col11(halt_2_out_13), .col12(halt_2_out_14),
    .col13(halt_2_out_15), .col14(halt_2_out_16), .col15(halt_2_out_17));
  Multiplexer #(.width(16)) multiplexer_3 (.in0(RT), .in1(Imm), .out(multiplexer_3_out), .sel(Itype));  // open: en
  Hex_Digit_Display hex_digit_display_3 (.value(display_1_digits_1));  // open: dp
  Hex_Digit_Display hex_digit_display_4 (.value(display_1_digits_2));  // open: dp
  Display display_1 (
    .Data(RS), .WE(put), .Digits_1(display_1_digits_1), .Digits_2(display_1_digits_2),
    .Digits_3(display_1_digits_3), .Digits_4(display_1_digits_4), .Clock(Clock));
  HALT halt_2 (
    .in_1(HALT), .out_2(halt_2_out_2), .out_3(halt_2_out_3), .out_4(halt_2_out_4), .out_5(halt_2_out_5),
    .out_6(halt_2_out_6), .out_7(halt_2_out_7), .out_8(halt_2_out_8), .out_9(halt_2_out_9),
    .out_10(halt_2_out_10), .out_11(halt_2_out_11), .out_12(halt_2_out_12), .out_13(halt_2_out_13),
    .out_14(halt_2_out_14), .out_15(halt_2_out_15), .out_16(halt_2_out_16), .out_17(halt_2_out_17));
  ALU alu_1 (.A(RS), .B(multiplexer_3_out), .Result(ALUout), .Remainder_Hi(Rem), .Operation(ALUOp), .WE(Rwe));

  // Notes on the sheet:
  //   PC
  //   Register File
  //   RAM Module
  //   CPU by Dane Halle
  //   ROM Module
  //   Control
  //   contents of rom_1 (hex, n*v repeats v):
  //   9e0e 9202 7200 9602 cc0c 6000 8603 22c1 7200 8fff ae0c 5c00
  //   ALU
endmodule

module register_file (
  input  Clock,
  input  [2:0] ReadRegister1,
  input  [2:0] ReadRegister2,
  input  [2:0] WriteRegister,
  input  [15:0] WireData,
  input  [15:0] WireData_1,
  input  WriteEnable,
  input  WriteEnable_1,
  output [15:0] ReadData1,
  output [15:0] ReadData2
);

  wire Read0a, Read0b, Read1a, Read1b, Read2a, Read2b, Read3a, Read3b, Read4a, Read4b, Read5a, Read5b,
       Read6a, Read6b, Read7a, Read7b, Write0, Write0_1, Write1, Write1_1, Write2, Write2_1, Write3,
       Write3_1, Write4, Write4_1, Write5, Write5_1, Write6, Write6_1, Write7, Write7_1;
  wire [2:0] WR_1;
  wire [15:0] controlled_buffer_1_out, controlled_buffer_3_out, controlled_buffer_5_out,
       controlled_buffer_7_out, controlled_buffer_17_out, controlled_buffer_19_out, controlled_buffer_21_out,
       controlled_buffer_23_out, register_1_q, register_2_q, register_3_q, register_4_q, register_5_q,
       register_6_q, register_7_q, register_8_q;

  // Decoder #(.select(3)) decoder_1: pin names not known; wires that end beside it: ReadRegister1, Read0a, Read1a, Read2a, Read3a, Read4a, Read5a, Read6a, Read7a
  // Decoder #(.select(3)) decoder_2: pin names not known; wires that end beside it: ReadRegister2, Read0b, Read1b, Read2b, Read3b, Read4b, Read5b, Read6b, Read7b
  // Demultiplexer #(.select(3)) demultiplexer_1: pin names not known; wires that end beside it: WriteEnable, WriteRegister, Write0, Write1, Write2, Write3, Write4, Write5, Write6, Write7
  // Demultiplexer #(.select(3)) demultiplexer_2: pin names not known; wires that end beside it: WriteEnable_1, WR_1, Write0_1, Write1_1, Write2_1, Write3_1, Write4_1, Write5_1, Write6_1, Write7_1
  assign controlled_buffer_1_out = Write0 ? WireData : 16'bz;  // Controlled_Buffer controlled_buffer_1
  Register #(.width(16)) register_1 (.D(controlled_buffer_1_out), .Q(register_1_q), .clk(Clock));  // open: en, clr
  assign controlled_buffer_1_out = Write0_1 ? WireData_1 : 16'bz;  // Controlled_Buffer controlled_buffer_2
  assign controlled_buffer_3_out = Write1 ? WireData : 16'bz;  // Controlled_Buffer controlled_buffer_3
  Register #(.width(16)) register_2 (.D(controlled_buffer_3_out), .Q(register_2_q), .clk(Clock));  // open: en, clr
  assign controlled_buffer_3_out = Write1_1 ? WireData_1 : 16'bz;  // Controlled_Buffer controlled_buffer_4
  assign controlled_buffer_5_out = Write2 ? WireData : 16'bz;  // Controlled_Buffer controlled_buffer_5
  Register #(.width(16)) register_3 (.D(controlled_buffer_5_out), .Q(register_3_q), .clk(Clock));  // open: en, clr
  assign controlled_buffer_5_out = Write2_1 ? WireData_1 : 16'bz;  // Controlled_Buffer controlled_buffer_6
  assign controlled_buffer_7_out = Write3 ? WireData : 16'bz;  // Controlled_Buffer controlled_buffer_7
  Register #(.width(16)) register_4 (.D(controlled_buffer_7_out), .Q(register_4_q), .clk(Clock));  // open: en, clr
  assign controlled_buffer_7_out = Write3_1 ? WireData_1 : 16'bz;  // Controlled_Buffer controlled_buffer_8
  assign ReadData1 = Read0a ? register_1_q : 16'bz;  // Controlled_Buffer controlled_buffer_9
  assign ReadData2 = Read0b ? register_1_q : 16'bz;  // Controlled_Buffer controlled_buffer_10
  assign ReadData1 = Read1a ? register_2_q : 16'bz;  // Controlled_Buffer controlled_buffer_11
  assign ReadData2 = Read1b ? register_2_q : 16'bz;  // Controlled_Buffer controlled_buffer_12
  assign ReadData1 = Read2a ? register_3_q : 16'bz;  // Controlled_Buffer controlled_buffer_13
  assign ReadData2 = Read2b ? register_3_q : 16'bz;  // Controlled_Buffer controlled_buffer_14
  assign ReadData1 = Read3a ? register_4_q : 16'bz;  // Controlled_Buffer controlled_buffer_15
  assign ReadData2 = Read3b ? register_4_q : 16'bz;  // Controlled_Buffer controlled_buffer_16
  assign controlled_buffer_17_out = Write4 ? WireData : 16'bz;  // Controlled_Buffer controlled_buffer_17
  assign controlled_buffer_17_out = Write4_1 ? WireData_1 : 16'bz;  // Controlled_Buffer controlled_buffer_18
  assign controlled_buffer_19_out = Write5 ? WireData : 16'bz;  // Controlled_Buffer controlled_buffer_19
  assign controlled_buffer_19_out = Write5_1 ? WireData_1 : 16'bz;  // Controlled_Buffer controlled_buffer_20
  assign controlled_buffer_21_out = Write6 ? WireData : 16'bz;  // Controlled_Buffer controlled_buffer_21
  assign controlled_buffer_21_out = Write6_1 ? WireData_1 : 16'bz;  // Controlled_Buffer controlled_buffer_22
  assign controlled_buffer_23_out = Write7 ? WireData : 16'bz;  // Controlled_Buffer controlled_buffer_23
  assign controlled_buffer_23_out = Write7_1 ? WireData_1 : 16'bz;  // Controlled_Buffer controlled_buffer_24
  Adder #(.width(3)) adder_1 (.a(WriteRegister), .b(3'b001), .out(WR_1));  // open: cin, cout
  assign ReadData1 = Read4a ? register_5_q : 16'bz;  // Controlled_Buffer controlled_buffer_25
  Register #(.width(16)) register_5 (.D(controlled_buffer_17_out), .Q(register_5_q), .clk(Clock));  // open: en, clr
  assign ReadData2 = Read4b ? register_5_q : 16'bz;  // Controlled_Buffer controlled_buffer_26
  assign ReadData1 = Read5a ? register_6_q : 16'bz;  // Controlled_Buffer controlled_buffer_27
  Register #(.width(16)) register_6 (.D(controlled_buffer_19_out), .Q(register_6_q), .clk(Clock));  // open: en, clr
  assign ReadData2 = Read5b ? register_6_q : 16'bz;  // Controlled_Buffer controlled_buffer_28
  assign ReadData1 = Read6a ? register_7_q : 16'bz;  // Controlled_Buffer controlled_buffer_29
  Register #(.width(16)) register_7 (.D(controlled_buffer_21_out), .Q(register_7_q), .clk(Clock));  // open: en, clr
  assign ReadData2 = Read6b ? register_7_q : 16'bz;  // Controlled_Buffer controlled_buffer_30
  assign ReadData1 = Read7a ? register_8_q : 16'bz;  // Controlled_Buffer controlled_buffer_31
  Register #(.width(16)) register_8 (.D(controlled_buffer_23_out), .Q(register_8_q), .clk(Clock));  // open: en, clr
  assign ReadData2 = Read7b ? register_8_q : 16'bz;  // Controlled_Buffer controlled_buffer_32

  // Other names for the same wires on the sheet: WR[2:0] = WriteRegister
endmodule

module ALU (
  input  [15:0] A,
  input  [15:0] B,
  input  [2:0] Operation,
  output [15:0] Result,
  output [15:0] Remainder_Hi,
  output WE
);

  wire and_2_p4, and_3_p4, and_4_out, and_5_p4;
  wire [15:0] ADD, AND, DIV, hi, MUL, NOR, rem, SL, SR, SUB;

  Adder #(.width(16)) adder_1 (.a(A), .b(B), .out(ADD));  // open: cin, cout
  assign NOR = ~(A | B);  // NOR_Gate nor_1, 16 bits wide
  Divider #(.width(16)) divider_1 (.a(A), .b(B), .out(DIV), .rem(rem));  // open: upper
  Shifter #(.width(16), .shift("lr")) shifter_1 (.in(A), .\dist (B[3:0]), .out(SR));
  Subtractor #(.width(16)) subtractor_1 (.a(A), .b(B), .out(SUB));  // open: bin, bout
  assign AND = A & B;  // AND_Gate and_1, 16 bits wide
  Multiplier #(.width(16)) multiplier_1 (.a(A), .b(B), .out(MUL), .cout(hi));  // open: cin
  Shifter #(.width(16)) shifter_2 (.in(A), .\dist (B[3:0]), .out(SL));
  Multiplexer #(.select(3), .width(16)) multiplexer_1 (
    .in0(ADD), .in1(SUB), .in2(AND), .in3(NOR), .in4(DIV), .in5(MUL), .in6(SR), .in7(SL), .out(Result),
    .sel(Operation));  // open: en
  Multiplexer #(.select(3), .width(16)) multiplexer_2 (
    .in4(rem), .in5(hi), .out(Remainder_Hi), .sel(Operation));  // open: in0, in1, in2, in3, in6, in7, en
  // AND_Gate and_2: pin names not known; wires that end beside it: Operation[1], Operation[0], Operation[1], and_2_p4
  // AND_Gate and_3: pin names not known; wires that end beside it: Operation[0], Operation[1], Operation[1], and_3_p4
  and and_4 (and_4_out, and_2_p4, Operation[2]);
  or or_1 (WE, and_4_out, and_4_out, and_5_p4, and_5_p4);
  // AND_Gate and_5: pin names not known; wires that end beside it: Operation[1], and_3_p4, Operation[2], and_5_p4

  // Other names for the same wires on the sheet: B_red[3:0] = B[3:0]; OP[2:0] = Operation
endmodule

module Control (
  input  [15:0] Instruction,
  input  [15:0] RSin,
  output [2:0] RS,
  output DoMem,
  output [2:0] RT,
  output [15:0] Immediate,
  output Halt,
  output Put,
  output I_Type,
  output [1:0] PC,
  output WriteEnable,
  output [2:0] WriteOp,
  output [2:0] ALUOp
);

  wire ADD, ADDi, ADDui, ALU, AND, and_1_out, and_2_p3, and_3_out, and_4_p7, and_5_out, bn, bp, bx, bz,
       demultiplexer_1_out10, demultiplexer_1_out11, demultiplexer_1_out12, demultiplexer_1_out13,
       demultiplexer_1_out14, demultiplexer_1_out15, demultiplexer_2_out2, demultiplexer_2_out3,
       demultiplexer_2_out8, demultiplexer_2_out9, demultiplexer_2_out10, demultiplexer_2_out11, DIV, j, jal,
       jr, li, lw, MUL, NOR, not_1_out, not_2_p4, not_3_out, or_4_out, or_8_out, RS_0, RS_0_t, RS_0_t_t,
       SLLV, SLRV, SUB, sw;
  wire [15:0] bit_extender_1_out, bit_extender_2_out;

  Demultiplexer #(.select(4)) demultiplexer_1 (
    .out0(ADD), .out1(SUB), .out2(AND), .out3(NOR), .out4(DIV), .out5(MUL), .out6(SLRV), .out7(SLLV),
    .out8(lw), .out9(sw), .out10(demultiplexer_1_out10), .out11(demultiplexer_1_out11),
    .out12(demultiplexer_1_out12), .out13(demultiplexer_1_out13), .out14(demultiplexer_1_out14),
    .out15(demultiplexer_1_out15), .in(not_1_out), .sel({Instruction[14:12], Instruction[0]}));  // open: en
  // NOT_Gate not_1 has open pins: in=open, out=not_1_out
  // OR_Gate or_1: pin names not known; wires that end beside it: demultiplexer_1_out14, demultiplexer_1_out15, demultiplexer_1_out15, Put
  // OR_Gate or_2: pin names not known; wires that end beside it: demultiplexer_1_out10, demultiplexer_1_out10, demultiplexer_1_out11, jr
  or or_3 (Halt, demultiplexer_1_out12, demultiplexer_1_out13, demultiplexer_1_out13);
  Comparator #(.width(16)) comparator_1 (.a(RSin), .b({16{1'b0}}), .gt(RS_0_t_t), .eq(RS_0_t), .lt(RS_0));
  Demultiplexer #(.select(4)) demultiplexer_2 (
    .out0(ADDui), .out1(ADDi), .out2(demultiplexer_2_out2), .out3(demultiplexer_2_out3), .out4(bp),
    .out5(bn), .out6(bx), .out7(bz), .out8(demultiplexer_2_out8), .out9(demultiplexer_2_out9),
    .out10(demultiplexer_2_out10), .out11(demultiplexer_2_out11), .in(Instruction[15]),
    .sel({Instruction[14:12], Instruction[0]}));  // open: out12, out13, out14, out15, en
  assign bit_extender_1_out = {{8{Instruction[8]}}, Instruction[8:1]};  // Bit_Extender bit_extender_1
  assign bit_extender_2_out = {{8{1'b0}}, Instruction[8:1]};  // Bit_Extender bit_extender_2
  or or_4 (or_4_out, li, ADDui);
  or or_5 (li, demultiplexer_2_out2, demultiplexer_2_out2, demultiplexer_2_out3);
  or or_6 (jal, demultiplexer_2_out8, demultiplexer_2_out8, demultiplexer_2_out9, demultiplexer_2_out10);
  or or_7 (j, demultiplexer_2_out9, demultiplexer_2_out10, demultiplexer_2_out11, demultiplexer_2_out11);
  Multiplexer #(.width(16)) multiplexer_1 (
    .in0(bit_extender_1_out), .in1(bit_extender_2_out), .out(Immediate), .sel(or_4_out));  // open: en
  and and_1 (and_1_out, RS_0, bn);
  // AND_Gate and_2: pin names not known; wires that end beside it: RS_0_t, bx, and_2_p3, bz, RS_0_t_t, bp
  buf and_3 (and_3_out, and_1_out);  // AND_Gate
  // AND_Gate and_4: pin names not known; wires that end beside it: bx, and_2_p3, RS_0_t, bz, RS_0_t_t, bp, and_4_p7
  // NOT_Gate not_2: pin names not known; wires that end beside it: ALU, Instruction[15], Instruction[15], not_2_p4
  and and_5 (and_5_out, Instruction[15], ALU);  // AND_Gate
  Priority_Encoder #(.select(2)) priority_encoder_1 (
    .in0(1'b1), .in1(or_8_out), .in2(jr), .out(PC));  // open: in3, gs, en_out, en_in
  or or_8 (or_8_out, jal, and_3_out, and_1_out, and_4_p7, and_2_p3, j);
  Priority_Encoder priority_encoder_2 (
    .in0(1'b1), .in1(not_2_p4), .in2(and_5_out), .in3(jal), .in4(lw), .out(WriteOp));  // open: in5, in6, in7, en_in, gs, en_out
  or or_9 (DoMem, lw, sw);
  or or_10 (ALU, ADD, SUB, AND, NOR, DIV, MUL, SLRV, SLLV, ADDui, ADDi);
  or or_11 (WriteEnable, ADD, SUB, AND, NOR, DIV, MUL, SLRV, SLLV, lw, ADDui, ADDi, li, jal);
  // NOT_Gate not_3 has open pins: in=open, out=not_3_out
  assign ALUOp = not_3_out ? {Instruction[13:12], Instruction[0]} : 3'bz;  // Controlled_Buffer controlled_buffer_1
  assign ALUOp = Instruction[15] ? 3'b000 : 3'bz;  // Controlled_Buffer controlled_buffer_2

  assign I_Type = Instruction[15];
  assign RS = Instruction[11:9];
  assign RT = Instruction[8:6];

  // Other names for the same wires on the sheet: _14 = Instruction[14]; OpCode[3:0] = Instruction[15:12];
  //   _0 = Instruction[0]; _12 = Instruction[12]; _13 = Instruction[13]; _1 = Instruction[1];
  //   Imm[7:0] = Instruction[8:1]; _2 = Instruction[2]; _3 = Instruction[3]; _4 = Instruction[4]; _5 = Instruction[5];
  //   _15 = Instruction[15]; _9 = Instruction[9]; _10 = Instruction[10]; _11 = Instruction[11]; _6 = Instruction[6];
  //   _7 = Instruction[7]; _8 = Instruction[8]
endmodule

module Display (
  input  [15:0] Data,
  input  WE,
  input  Clock,
  output [3:0] Digits_1,
  output [3:0] Digits_2,
  output [3:0] Digits_3,
  output [3:0] Digits_4
);

  Register #(.width(16)) register_1 (
    .D(Data), .en(WE), .Q({Digits_4, Digits_3, Digits_2, Digits_1}), .clk(Clock));  // open: clr
endmodule

module HALT (
  input  in_1,
  output [6:0] out_2,
  output [6:0] out_3,
  output [6:0] out_4,
  output [6:0] out_5,
  output [6:0] out_6,
  output [6:0] out_7,
  output [6:0] out_8,
  output [6:0] out_9,
  output [6:0] out_10,
  output [6:0] out_11,
  output [6:0] out_12,
  output [6:0] out_13,
  output [6:0] out_14,
  output [6:0] out_15,
  output [6:0] out_16,
  output [6:0] out_17
);

  wire not_1_out, not_2_out, not_3_out, not_4_out;

  assign {out_5, out_4, out_3, out_2} = not_1_out ? 28'h3889f00 : 28'bz;  // Controlled_Buffer controlled_buffer_1
  // NOT_Gate not_1 has open pins: in=open, out=not_1_out
  assign {out_5, out_4, out_3, out_2} = in_1 ? 28'h7c21f00 : 28'bz;  // Controlled_Buffer controlled_buffer_2
  assign {out_9, out_8, out_7, out_6} = not_2_out ? 28'h3ca0f00 : 28'bz;  // Controlled_Buffer controlled_buffer_3
  // NOT_Gate not_2 has open pins: in=open, out=not_2_out
  assign {out_9, out_8, out_7, out_6} = in_1 ? 28'h3ca0f00 : 28'bz;  // Controlled_Buffer controlled_buffer_4
  assign {out_14, out_15, out_16, out_17} = not_3_out ? 28'hf9500 : 28'bz;  // Controlled_Buffer controlled_buffer_5
  // NOT_Gate not_3 has open pins: in=open, out=not_3_out
  assign {out_14, out_15, out_16, out_17} = in_1 ? 28'h40f9000 : 28'bz;  // Controlled_Buffer controlled_buffer_6
  assign {out_10, out_11, out_12, out_13} = not_4_out ? 28'hf8c3e : 28'bz;  // Controlled_Buffer controlled_buffer_7
  // NOT_Gate not_4 has open pins: in=open, out=not_4_out
  assign {out_10, out_11, out_12, out_13} = in_1 ? 28'hf8102 : 28'bz;  // Controlled_Buffer controlled_buffer_8

  // Other names for the same wires on the sheet: HALT = in_1

  // Notes on the sheet:
  //   This is basically what I did when I was bored and needed a break from debugging
endmodule
